// Logisim project PSG.circ as structural Verilog: 5 circuits, main circuit main
module main (
  input  FCLK,
  input  CLK,
  input  D0,
  input  D1,
  input  D2,
  input  D3,
  input  A0,
  input  WR,
  input  RST,
  output S0,
  output S1,
  output S2,
  output S3,
  output S4,
  output S5,
  output LED0,
  output LED1
);

  wire adder_1_cout, and_1_out, and_2_out, and_3_out, and_6_out, and_7_out, d_ff_1_q, d_ff_1_qn, d_ff_2_qn,
       d_ff_3_qn, d_ff_4_q, d_ff_4_qn, d_ff_5_qn, d_ff_6_qn, d_ff_7_qn, d_ff_8_qn, d_ff_9_qn,
       demultiplexer_1_out1, demultiplexer_1_out2, demultiplexer_1_out3, demultiplexer_1_out4,
       demultiplexer_1_out5, demultiplexer_1_out6, demultiplexer_1_out7, demultiplexer_1_out8,
       demultiplexer_1_out9, demultiplexer_1_out10, demultiplexer_1_out11, demultiplexer_1_out12,
       demultiplexer_1_out13, demultiplexer_1_out14, demultiplexer_1_out15, not_1_out,
       tone_generator_2_1_sout, tone_generator_2_2_sout, triangle_wave_generator_1_d0,
       triangle_wave_generator_1_d1, triangle_wave_generator_1_d2, triangle_wave_generator_1_d3;
  wire [3:0] and_5_out, and_8_out, register_1_q, register_2_q, tone_generator_1_dout;
  wire [3:3] and_4_out;
  wire [5:0] and_9_out;

  and and_1 (and_1_out, FCLK, d_ff_9_qn);
  not not_1 (not_1_out, A0);
  and and_2 (and_2_out, CLK, RST);
  D_Flip_Flop d_ff_1 (.D(d_ff_1_qn), .clk(and_1_out), .Q(d_ff_1_q), .Qn(d_ff_1_qn), .reset(CLK));  // open: preset
  D_Flip_Flop d_ff_2 (.D(d_ff_2_qn), .clk(d_ff_1_qn), .Qn(d_ff_2_qn), .reset(CLK));  // open: Q, preset
  D_Flip_Flop d_ff_3 (.D(d_ff_3_qn), .clk(d_ff_2_qn), .Qn(d_ff_3_qn), .reset(CLK));  // open: Q, preset
  D_Flip_Flop d_ff_4 (.D(d_ff_4_qn), .clk(d_ff_3_qn), .Q(d_ff_4_q), .Qn(d_ff_4_qn), .reset(CLK));  // open: preset
  D_Flip_Flop d_ff_5 (.D(d_ff_5_qn), .clk(d_ff_4_qn), .Qn(d_ff_5_qn), .reset(CLK));  // open: Q, preset
  D_Flip_Flop d_ff_6 (.D(d_ff_6_qn), .clk(d_ff_5_qn), .Qn(d_ff_6_qn), .reset(CLK));  // open: Q, preset
  D_Flip_Flop d_ff_7 (.D(d_ff_7_qn), .clk(d_ff_6_qn), .Qn(d_ff_7_qn), .reset(CLK));  // open: Q, preset
  D_Flip_Flop d_ff_8 (.D(d_ff_8_qn), .clk(d_ff_7_qn), .Qn(d_ff_8_qn), .reset(CLK));  // open: Q, preset
  D_Flip_Flop d_ff_9 (.D(d_ff_9_qn), .clk(d_ff_8_qn), .Qn(d_ff_9_qn), .reset(CLK));  // open: Q, preset
  Register #(.width(4)) register_1 (.D({D3, D2, D1, D0}), .en(and_3_out), .clk(CLK), .Q(register_1_q));  // open: clr
  and and_3 (and_3_out, not_1_out, WR);
  and and_4 (and_4_out[3], WR, A0);
  Demultiplexer #(.select(4)) demultiplexer_1 (
    .out1(demultiplexer_1_out1), .out2(demultiplexer_1_out2), .out3(demultiplexer_1_out3),
    .out4(demultiplexer_1_out4), .out5(demultiplexer_1_out5), .out6(demultiplexer_1_out6),
    .out7(demultiplexer_1_out7), .out8(demultiplexer_1_out8), .out9(demultiplexer_1_out9),
    .out10(demultiplexer_1_out10), .out11(demultiplexer_1_out11), .out12(demultiplexer_1_out12),
    .out13(demultiplexer_1_out13), .out14(demultiplexer_1_out14), .out15(demultiplexer_1_out15), .in(1'b1),
    .sel(and_5_out));  // open: out0
  assign and_5_out = register_1_q & {4{and_4_out[3]}};  // AND_Gate and_5, 4 bits wide
  Register #(.width(4)) register_2 (
    .D({D3, D2, D1, D0}), .en(demultiplexer_1_out15), .clk(CLK), .Q(register_2_q), .clr(and_2_out));
  tone_generator_2 tone_generator_2_2 (
    .FCLK(and_1_out), .FCLK_16(d_ff_4_q), .RST_C(and_2_out), .DIN({D3, D2, D1, D0}),
    .LSEL(demultiplexer_1_out1), .CLK(CLK), .HSEL(demultiplexer_1_out2), .HHSEL(demultiplexer_1_out3),
    .SOUT(tone_generator_2_2_sout));
  tone_generator_2 tone_generator_2_1 (
    .FCLK(and_1_out), .FCLK_16(d_ff_4_q), .RST_C(and_2_out), .DIN({D3, D2, D1, D0}),
    .LSEL(demultiplexer_1_out4), .CLK(CLK), .HSEL(demultiplexer_1_out5), .HHSEL(demultiplexer_1_out6),
    .SOUT(tone_generator_2_1_sout));
  triangle_wave_generator triangle_wave_generator_1 (
    .FCLK(and_1_out), .FCLK_16(d_ff_1_q), .RST_C(and_2_out), .DIN({D3, D2, D1, D0}),
    .LSEL(demultiplexer_1_out7), .CLK(CLK), .HSEL(demultiplexer_1_out8), .HHSEL(demultiplexer_1_out9),
    .D3(triangle_wave_generator_1_d3), .D2(triangle_wave_generator_1_d2), .D1(triangle_wave_generator_1_d1),
    .D0(triangle_wave_generator_1_d0));
  tone_generator tone_generator_1 (
    .FCLK(and_1_out), .FCLK_16(d_ff_1_q), .RST_C(and_2_out), .DIN({D3, D2, D1, D0}),
    .LSEL(demultiplexer_1_out10), .CLK(CLK), .HSEL(demultiplexer_1_out11), .HHSEL(demultiplexer_1_out12),
    .DOUT(tone_generator_1_dout));
  and and_6 (and_6_out, tone_generator_2_2_sout, register_2_q[0]);
  and and_7 (and_7_out, tone_generator_2_1_sout, register_2_q[1]);
  assign and_8_out = tone_generator_1_dout & {4{register_2_q[3]}};  // AND_Gate and_8, 4 bits wide
  and and_9 (and_9_out[0], triangle_wave_generator_1_d0, register_2_q[2]);
  and and_10 (and_9_out[1], triangle_wave_generator_1_d1, register_2_q[2]);
  and and_11 (and_9_out[2], triangle_wave_generator_1_d2, register_2_q[2]);
  and and_12 (and_9_out[3], triangle_wave_generator_1_d3, register_2_q[2]);
  xor xor_1 (and_9_out[4], and_6_out, and_7_out);
  and and_13 (and_9_out[5], and_6_out, and_7_out);
  Adder #(.width(6)) adder_1 (
    .a(and_9_out), .b({2'b00, and_8_out}), .out({S5, S4, S3, S2, S1, S0}), .cin(1'b0), .cout(adder_1_cout));
  // NoConnect on adder_1_cout
  D_Flip_Flop d_ff_10 (.D(D0), .clk(demultiplexer_1_out13), .Q(LED0));  // open: Qn, preset, reset
  D_Flip_Flop d_ff_11 (.D(D0), .clk(demultiplexer_1_out14), .Q(LED1));  // open: Qn, preset, reset
endmodule

module tone_generator (
  input  FCLK,
  input  FCLK_16,
  input  RST_C,
  input  [3:0] DIN,
  input  LSEL,
  input  CLK,
  input  HSEL,
  input  HHSEL,
  output [3:0] DOUT
);

  wire d_ff_1_q, d_ff_2_q, d_ff_3_q, d_ff_4_q, d_ff_5_q, d_ff_6_q, d_ff_7_q, d_ff_8_q, d_ff_9_q, d_ff_11_q,
       d_ff_12_q, d_ff_14_q, tone_generator_2_1_sout, xor_1_out, xor_2_out, xor_3_out;
  wire [3:0] d_ff_16_q;

  tone_generator_2 tone_generator_2_1 (
    .FCLK(FCLK), .FCLK_16(FCLK_16), .RST_C(RST_C), .DIN(DIN), .LSEL(LSEL), .CLK(CLK), .HSEL(HSEL),
    .HHSEL(HHSEL), .SOUT(tone_generator_2_1_sout));
  D_Flip_Flop d_ff_1 (.D(d_ff_16_q[0]), .clk(FCLK_16), .Q(d_ff_1_q));  // open: Qn, preset, reset
  Register #(.width(4)) register_1 (.D(d_ff_16_q), .en(1'b1), .clk(tone_generator_2_1_sout), .Q(DOUT));  // open: clr
  D_Flip_Flop d_ff_2 (.D(d_ff_1_q), .clk(FCLK_16), .Q(d_ff_2_q));  // open: Qn, preset, reset
  xor xor_1 (xor_1_out, d_ff_2_q, d_ff_16_q[0]);
  D_Flip_Flop d_ff_3 (.D(xor_1_out), .clk(FCLK_16), .Q(d_ff_3_q));  // open: Qn, preset, reset
  D_Flip_Flop d_ff_4 (.D(xor_2_out), .clk(FCLK_16), .Q(d_ff_4_q));  // open: Qn, preset, reset
  xor xor_2 (xor_2_out, d_ff_3_q, d_ff_16_q[0]);
  D_Flip_Flop d_ff_5 (.D(d_ff_4_q), .clk(FCLK_16), .Q(d_ff_5_q));  // open: Qn, preset, reset
  D_Flip_Flop d_ff_6 (.D(xor_3_out), .clk(FCLK_16), .Q(d_ff_6_q));  // open: Qn, preset, reset
  xor xor_3 (xor_3_out, d_ff_5_q, d_ff_16_q[0]);
  D_Flip_Flop d_ff_7 (.D(d_ff_6_q), .clk(FCLK_16), .Q(d_ff_7_q));  // open: Qn, preset, reset
  D_Flip_Flop d_ff_8 (.D(d_ff_7_q), .clk(FCLK_16), .Q(d_ff_8_q), .preset(RST_C));  // open: Qn, reset
  D_Flip_Flop d_ff_9 (.D(d_ff_8_q), .clk(FCLK_16), .Q(d_ff_9_q), .reset(RST_C));  // open: Qn, preset
  D_Flip_Flop d_ff_10 (.D(d_ff_9_q), .clk(FCLK_16), .Q(d_ff_16_q[3]), .preset(RST_C));  // open: Qn, reset
  D_Flip_Flop d_ff_11 (.D(d_ff_16_q[3]), .clk(FCLK_16), .Q(d_ff_11_q), .reset(RST_C));  // open: Qn, preset
  D_Flip_Flop d_ff_12 (.D(d_ff_11_q), .clk(FCLK_16), .Q(d_ff_12_q), .preset(RST_C));  // open: Qn, reset
  D_Flip_Flop d_ff_13 (.D(d_ff_12_q), .clk(FCLK_16), .Q(d_ff_16_q[2]), .reset(RST_C));  // open: Qn, preset
  D_Flip_Flop d_ff_14 (.D(d_ff_16_q[2]), .clk(FCLK_16), .Q(d_ff_14_q), .preset(RST_C));  // open: Qn, reset
  D_Flip_Flop d_ff_15 (.D(d_ff_14_q), .clk(FCLK_16), .Q(d_ff_16_q[1]), .preset(RST_C));  // open: Qn, reset
  D_Flip_Flop d_ff_16 (.D(d_ff_16_q[1]), .clk(FCLK_16), .Q(d_ff_16_q[0]), .reset(RST_C));  // open: Qn, preset
endmodule

module tone_generator_2 (
  input  FCLK,
  input  FCLK_16,
  input  RST_C,
  input  [3:0] DIN,
  input  LSEL,
  input  CLK,
  input  HSEL,
  input  HHSEL,
  output SOUT
);

  wire and_1_out, and_2_out, and_3_out, and_4_out, and_5_out, and_6_out, and_7_out, and_8_out, and_9_out,
       and_10_out, and_11_out, and_12_out, d_ff_1_q, d_ff_1_qn, d_ff_2_q, d_ff_2_qn, d_ff_3_q, d_ff_3_qn,
       d_ff_4_q, d_ff_4_qn, d_ff_5_q, d_ff_5_qn, d_ff_6_q, d_ff_6_qn, d_ff_7_q, d_ff_7_qn, d_ff_8_q,
       d_ff_8_qn, d_ff_9_q, d_ff_9_qn, d_ff_10_q, d_ff_10_qn, d_ff_11_q, d_ff_11_qn, d_ff_12_qn, not_1_out,
       or_1_out, or_2_out, or_3_out, xnor_1_out, xnor_2_out, xnor_3_out, xnor_4_out, xnor_5_out, xnor_6_out,
       xnor_7_out, xnor_8_out, xnor_9_out, xnor_10_out, xnor_11_out, xor_1_out;
  wire [2:0] register_3_q;
  wire [3:0] register_1_q, register_2_q;

  Register #(.width(4)) register_1 (.D(DIN), .en(LSEL), .clk(CLK), .Q(register_1_q));  // open: clr
  Register #(.width(4)) register_2 (.D(DIN), .en(HSEL), .clk(CLK), .Q(register_2_q));  // open: clr
  Register #(.width(3)) register_3 (.D(DIN[2:0]), .en(HHSEL), .clk(CLK), .Q(register_3_q));  // open: clr
  or or_1 (or_1_out, LSEL, HSEL);
  or or_2 (or_2_out, or_1_out, HHSEL);
  and and_1 (and_1_out, CLK, or_2_out);
  not not_1 (not_1_out, FCLK);
  and and_2 (and_2_out, not_1_out, and_12_out);
  D_Flip_Flop d_ff_1 (.D(d_ff_1_qn), .clk(FCLK_16), .Q(d_ff_1_q), .Qn(d_ff_1_qn), .reset(xor_1_out));  // open: preset
  D_Flip_Flop d_ff_2 (.D(d_ff_2_qn), .clk(d_ff_1_qn), .Q(d_ff_2_q), .Qn(d_ff_2_qn), .reset(xor_1_out));  // open: preset
  D_Flip_Flop d_ff_3 (.D(d_ff_3_qn), .clk(d_ff_2_qn), .Q(d_ff_3_q), .Qn(d_ff_3_qn), .reset(xor_1_out));  // open: preset
  D_Flip_Flop d_ff_4 (.D(d_ff_4_qn), .clk(d_ff_3_qn), .Q(d_ff_4_q), .Qn(d_ff_4_qn), .reset(xor_1_out));  // open: preset
  D_Flip_Flop d_ff_5 (.D(d_ff_5_qn), .clk(d_ff_4_qn), .Q(d_ff_5_q), .Qn(d_ff_5_qn), .reset(xor_1_out));  // open: preset
  D_Flip_Flop d_ff_6 (.D(d_ff_6_qn), .clk(d_ff_5_qn), .Q(d_ff_6_q), .Qn(d_ff_6_qn), .reset(xor_1_out));  // open: preset
  D_Flip_Flop d_ff_7 (.D(d_ff_7_qn), .clk(d_ff_6_qn), .Q(d_ff_7_q), .Qn(d_ff_7_qn), .reset(xor_1_out));  // open: preset
  D_Flip_Flop d_ff_8 (.D(d_ff_8_qn), .clk(d_ff_7_qn), .Q(d_ff_8_q), .Qn(d_ff_8_qn), .reset(xor_1_out));  // open: preset
  D_Flip_Flop d_ff_9 (.D(d_ff_9_qn), .clk(d_ff_8_qn), .Q(d_ff_9_q), .Qn(d_ff_9_qn), .reset(xor_1_out));  // open: preset
  D_Flip_Flop d_ff_10 (
    .D(d_ff_10_qn), .clk(d_ff_9_qn), .Q(d_ff_10_q), .Qn(d_ff_10_qn), .reset(xor_1_out));  // open: preset
  D_Flip_Flop d_ff_11 (
    .D(d_ff_11_qn), .clk(d_ff_10_qn), .Q(d_ff_11_q), .Qn(d_ff_11_qn), .reset(xor_1_out));  // open: preset
  xor xor_1 (xor_1_out, or_3_out, RST_C);
  or or_3 (or_3_out, and_2_out, and_1_out);
  xnor xnor_1 (xnor_1_out, d_ff_1_q, register_1_q[0]);
  xnor xnor_2 (xnor_2_out, d_ff_2_q, register_1_q[1]);
  xnor xnor_3 (xnor_3_out, d_ff_3_q, register_1_q[2]);
  xnor xnor_4 (xnor_4_out, d_ff_4_q, register_1_q[3]);
  xnor xnor_5 (xnor_5_out, d_ff_5_q, register_2_q[0]);
  xnor xnor_6 (xnor_6_out, d_ff_6_q, register_2_q[1]);
  xnor xnor_7 (xnor_7_out, d_ff_7_q, register_2_q[2]);
  xnor xnor_8 (xnor_8_out, d_ff_8_q, register_2_q[3]);
  xnor xnor_9 (xnor_9_out, d_ff_9_q, register_3_q[0]);
  xnor xnor_10 (xnor_10_out, d_ff_10_q, register_3_q[1]);
  xnor xnor_11 (xnor_11_out, d_ff_11_q, register_3_q[2]);
  and and_3 (and_3_out, xnor_1_out, xnor_2_out);
  and and_4 (and_4_out, xnor_3_out, xnor_4_out);
  and and_5 (and_5_out, xnor_5_out, xnor_6_out);
  and and_6 (and_6_out, xnor_7_out, xnor_8_out);
  and and_7 (and_7_out, xnor_9_out, xnor_10_out);
  and and_8 (and_8_out, and_3_out, and_4_out);
  and and_9 (and_9_out, and_5_out, and_6_out);
  and and_10 (and_10_out, and_7_out, xnor_11_out);
  and and_11 (and_11_out, and_9_out, and_10_out);
  and and_12 (and_12_out, and_8_out, and_11_out);
  D_Flip_Flop d_ff_12 (.D(d_ff_12_qn), .clk(and_12_out), .Q(SOUT), .Qn(d_ff_12_qn));  // open: preset, reset
endmodule

module test (
);

  wire button_1_out, clock_1_out, clock_2_out, dipswitch_1_p1, dipswitch_1_p2, dipswitch_1_p3,
       dipswitch_1_p4, dipswitch_1_p5, dipswitch_1_p6, dipswitch_1_p7, main_1_s0, or_1_out;

  Button button_1 (.out(button_1_out));
  Clock #(.highDuration(5), .lowDuration(514)) clock_1 (.out(clock_1_out));
  or or_1 (or_1_out, button_1_out, clock_1_out);
  Clock clock_2 (.out(clock_2_out));
  // DipSwitch dipswitch_1: pin names not known; wires that end beside it: dipswitch_1_p1, dipswitch_1_p2, dipswitch_1_p3, dipswitch_1_p4, dipswitch_1_p5, dipswitch_1_p6, dipswitch_1_p7
  main main_1 (
    .FCLK(clock_2_out), .CLK(or_1_out), .D0(dipswitch_1_p7), .D1(dipswitch_1_p6), .D2(dipswitch_1_p5),
    .D3(dipswitch_1_p4), .A0(dipswitch_1_p2), .WR(dipswitch_1_p1), .RST(dipswitch_1_p3), .S0(main_1_s0));  // open: S1, S2, S3, S4, S5, LED0, LED1
  LED led_1 (.in(main_1_s0));
endmodule

module triangle_wave_generator (
  input  FCLK,
  input  FCLK_16,
  input  RST_C,
  input  [3:0] DIN,
  input  LSEL,
  input  CLK,
  input  HSEL,
  input  HHSEL,
  output D3,
  output D2,
  output D1,
  output D0
);

  wire and_1_out, and_2_out, and_3_out, and_4_out, and_5_out, and_6_out, and_7_out, and_8_out, and_9_out,
       and_10_out, and_11_out, and_12_out, d_ff_1_q, d_ff_1_qn, d_ff_2_q, d_ff_2_qn, d_ff_3_q, d_ff_3_qn,
       d_ff_4_q, d_ff_4_qn, d_ff_5_q, d_ff_5_qn, d_ff_6_q, d_ff_6_qn, d_ff_7_q, d_ff_7_qn, d_ff_8_q,
       d_ff_8_qn, d_ff_9_q, d_ff_9_qn, d_ff_10_q, d_ff_10_qn, d_ff_11_q, d_ff_11_qn, d_ff_12_qn, d_ff_13_qn,
       d_ff_14_qn, d_ff_15_qn, not_1_out, or_1_out, or_2_out, or_3_out, xnor_1_out, xnor_2_out, xnor_3_out,
       xnor_4_out, xnor_5_out, xnor_6_out, xnor_7_out, xnor_8_out, xnor_9_out, xnor_10_out, xnor_11_out,
       xor_1_out;
  wire [2:0] register_3_q;
  wire [3:0] register_1_q, register_2_q;

  Register #(.width(4)) register_1 (.D(DIN), .en(LSEL), .clk(CLK), .Q(register_1_q));  // open: clr
  Register #(.width(4)) register_2 (.D(DIN), .en(HSEL), .clk(CLK), .Q(register_2_q));  // open: clr
  Register #(.width(3)) register_3 (.D(DIN[2:0]), .en(HHSEL), .clk(CLK), .Q(register_3_q));  // open: clr
  or or_1 (or_1_out, LSEL, HSEL);
  or or_2 (or_2_out, or_1_out, HHSEL);
  and and_1 (and_1_out, CLK, or_2_out);
  not not_1 (not_1_out, FCLK);
  and and_2 (and_2_out, not_1_out, and_12_out);
  D_Flip_Flop d_ff_1 (.D(d_ff_1_qn), .clk(FCLK_16), .Q(d_ff_1_q), .Qn(d_ff_1_qn), .reset(xor_1_out));  // open: preset
  D_Flip_Flop d_ff_2 (.D(d_ff_2_qn), .clk(d_ff_1_qn), .Q(d_ff_2_q), .Qn(d_ff_2_qn), .reset(xor_1_out));  // open: preset
  D_Flip_Flop d_ff_3 (.D(d_ff_3_qn), .clk(d_ff_2_qn), .Q(d_ff_3_q), .Qn(d_ff_3_qn), .reset(xor_1_out));  // open: preset
  D_Flip_Flop d_ff_4 (.D(d_ff_4_qn), .clk(d_ff_3_qn), .Q(d_ff_4_q), .Qn(d_ff_4_qn), .reset(xor_1_out));  // open: preset
  D_Flip_Flop d_ff_5 (.D(d_ff_5_qn), .clk(d_ff_4_qn), .Q(d_ff_5_q), .Qn(d_ff_5_qn), .reset(xor_1_out));  // open: preset
  D_Flip_Flop d_ff_6 (.D(d_ff_6_qn), .clk(d_ff_5_qn), .Q(d_ff_6_q), .Qn(d_ff_6_qn), .reset(xor_1_out));  // open: preset
  D_Flip_Flop d_ff_7 (.D(d_ff_7_qn), .clk(d_ff_6_qn), .Q(d_ff_7_q), .Qn(d_ff_7_qn), .reset(xor_1_out));  // open: preset
  D_Flip_Flop d_ff_8 (.D(d_ff_8_qn), .clk(d_ff_7_qn), .Q(d_ff_8_q), .Qn(d_ff_8_qn), .reset(xor_1_out));  // open: preset
  D_Flip_Flop d_ff_9 (.D(d_ff_9_qn), .clk(d_ff_8_qn), .Q(d_ff_9_q), .Qn(d_ff_9_qn), .reset(xor_1_out));  // open: preset
  D_Flip_Flop d_ff_10 (
    .D(d_ff_10_qn), .clk(d_ff_9_qn), .Q(d_ff_10_q), .Qn(d_ff_10_qn), .reset(xor_1_out));  // open: preset
  D_Flip_Flop d_ff_11 (
    .D(d_ff_11_qn), .clk(d_ff_10_qn), .Q(d_ff_11_q), .Qn(d_ff_11_qn), .reset(xor_1_out));  // open: preset
  xor xor_1 (xor_1_out, or_3_out, RST_C);
  or or_3 (or_3_out, and_2_out, and_1_out);
  xnor xnor_1 (xnor_1_out, d_ff_1_q, register_1_q[0]);
  xnor xnor_2 (xnor_2_out, d_ff_2_q, register_1_q[1]);
  xnor xnor_3 (xnor_3_out, d_ff_3_q, register_1_q[2]);
  xnor xnor_4 (xnor_4_out, d_ff_4_q, register_1_q[3]);
  xnor xnor_5 (xnor_5_out, d_ff_5_q, register_2_q[0]);
  xnor xnor_6 (xnor_6_out, d_ff_6_q, register_2_q[1]);
  xnor xnor_7 (xnor_7_out, d_ff_7_q, register_2_q[2]);
  xnor xnor_8 (xnor_8_out, d_ff_8_q, register_2_q[3]);
  xnor xnor_9 (xnor_9_out, d_ff_9_q, register_3_q[0]);
  xnor xnor_10 (xnor_10_out, d_ff_10_q, register_3_q[1]);
  xnor xnor_11 (xnor_11_out, d_ff_11_q, register_3_q[2]);
  and and_3 (and_3_out, xnor_1_out, xnor_2_out);
  and and_4 (and_4_out, xnor_3_out, xnor_4_out);
  and and_5 (and_5_out, xnor_5_out, xnor_6_out);
  and and_6 (and_6_out, xnor_7_out, xnor_8_out);
  and and_7 (and_7_out, xnor_9_out, xnor_10_out);
  and and_8 (and_8_out, and_3_out, and_4_out);
  and and_9 (and_9_out, and_5_out, and_6_out);
  and and_10 (and_10_out, and_7_out, xnor_11_out);
  and and_11 (and_11_out, and_9_out, and_10_out);
  and and_12 (and_12_out, and_8_out, and_11_out);
  D_Flip_Flop d_ff_12 (.D(d_ff_12_qn), .clk(d_ff_13_qn), .Q(D3), .Qn(d_ff_12_qn));  // open: preset, reset
  D_Flip_Flop d_ff_13 (.D(d_ff_13_qn), .clk(d_ff_14_qn), .Q(D2), .Qn(d_ff_13_qn));  // open: preset, reset
  D_Flip_Flop d_ff_14 (.D(d_ff_14_qn), .clk(d_ff_15_qn), .Q(D1), .Qn(d_ff_14_qn));  // open: preset, reset
  D_Flip_Flop d_ff_15 (.D(d_ff_15_qn), .clk(and_12_out), .Q(D0), .Qn(d_ff_15_qn));  // open: preset, reset
endmodule
